# Fritzing sketch RADIO TEA5767 (saved by Fritzing 0.9.3b)
breadboards: 1

parts:
  Tiny_RTC1 = Tiny RTC
  Squix1 = OLED 0.96" 128x64 I2C SSD1306
  RE1 = KY-040 Rotary encoder [package=THT]
  M1 = TEA5767 [package=THT]
  Componente1 = Arduino Nano (Rev3.0)
  R1 = Resistor [tolerance=±5% resistance=4.7k package="0603 [SMD]"]
  R2 = Resistor [tolerance=±5% resistance=4.7k package="0603 [SMD]"]

nets:
  N1: Tiny_RTC1.SCL, Squix1.SCL, M1.pin3, Componente1.A5, R2.Pin_1
  N2: Tiny_RTC1.SDA, Squix1.SCA, M1.pin2, Componente1.A4, R1.Pin_1
  VCC: Tiny_RTC1.VCC, Squix1.VCC, RE1.Vcc, M1.pin1, Componente1.5V, R1.Pin_0, R2.Pin_0
  GND: Tiny_RTC1.GND, Squix1.GND, RE1.GND, M1.pin4, Componente1.GND
  N3: RE1.DT, Componente1.A2
  N4: RE1.CLK, Componente1.A3

custom parts:
  Tiny RTC: Tiny RTC I2C module DS1370Z RTC and AT24C32 EEPROM
  KY-040 Rotary encoder: KY-040 Rotary Encoder with switch on breakout borad from AZ Delivery
  TEA5767: SMAKN brand new 76-108MHZ 5V TEA5767 FM Stereo Radio Module with Cable Antenna for Arduino EK1705(New version)
